// Logisim project multiplication.circ as structural Verilog: 1 circuit, main circuit main
module main (
  input  _1,
  input  _2,
  input  _4,
  input  _8,
  input  _1_2,
  input  _2_2,
  input  _4_2,
  input  _8_2,
  output _1_3,
  output _2_3,
  output _3,
  output _4_3,
  output _5,
  output _6,
  output _7,
  output _8_3,
  output _9,
  output _10,
  output out_19,
  output out_20,
  output _15,
  output _16,
  output _18,
  output _20,
  output _21,
  output _24,
  output _25,
  output _28,
  output _30,
  output _32,
  output _35,
  output _36,
  output _40,
  output _42,
  output _48,
  output _49,
  output _56,
  output _64
);

  wire _2_2_out, _2_out, _3_2_out, _3_3_out, _3_4_out, _3_out, _4_2_out, _4_3_out, _4_out, _5_2_out,
       _5_3_out, _5_4_out, _5_out, _6_2_out, _6_3_out, _6_4_out, _6_6_out, _6_out, _7_2_out, _7_3_out,
       _7_4_out, _7_out, _8_2_out, _8_3_out, _8_4_out, _8_out, _10_2_out, _10_out, _12_3_out, _12_4_out,
       _14_2_out, _14_out, _15_2_out, _15_out, _16_2_out, _16_3_out, _16_out, _18_2_out, _18_out, _20_2_out,
       _20_out, _21_2_out, _21_out, _24_2_out, _24_3_out, _24_4_out, _28_2_out, _28_out, _30_2_out, _30_out,
       _32_2_out, _32_out, _35_2_out, _35_out, _40_2_out, _40_out, _42_2_out, _42_out, _48_2_out, _48_out,
       _56_2_out, _56_out, and_1_out, and_2_out, and_3_out, and_4_out, and_5_out, and_6_out, and_7_out,
       and_8_out, and_9_out, and_10_out, and_11_out, and_12_out, and_13_out, and_14_out, and_15_out,
       and_16_out, and_17_out, and_18_out, and_19_out, and_20_out, and_21_out, and_22_out, and_23_out,
       and_24_out, and_25_out, and_26_out, and_27_out, and_28_out, and_29_out, and_30_out, and_31_out,
       and_32_out, and_33_out, and_34_out, and_35_out, and_36_out, and_37_out, and_38_out, and_39_out,
       and_40_out, and_41_out, and_42_out, and_43_out, and_44_out, and_45_out, and_46_out, and_47_out,
       and_48_out, and_49_out, and_50_out, and_51_out, and_52_out, and_53_out, and_54_out, and_55_out,
       and_56_out, and_57_out, and_58_out, and_59_out, and_60_out, and_61_out, and_62_out, and_63_out,
       and_64_out, or_1_out, or_5_out, or_8_out, or_11_out, or_12_out, or_17_out, or_18_out, xor_1_out,
       xor_2_out, xor_3_out, xor_4_out, xor_5_out, xor_6_out, xor_7_out, xor_8_out, xor_9_out, xor_10_out,
       xor_11_out, xor_12_out, xor_13_out;

  or or_1 (or_1_out, _2_2, _1_2, _4_2);
  ExactlyOne xor_1 (.out(xor_1_out), .in1(_8_2), .in3(_8_2), .in4(_7_out));
  ExactlyOne xor_2 (.out(xor_2_out), .in0(or_1_out), .in1(or_1_out), .in2(_8_2));
  and u__6 (_6_out, _2_2, _4_2);
  and u__7 (_7_out, _4_2, _2_2, _1_2);
  xor xor_3 (xor_3_out, xor_1_out, _6_out);
  ExactlyOne xor_4 (.out(xor_4_out), .in1(_8_2), .in3(xor_3_out), .in4(_8_2));
  and u__5 (_5_out, _4_2, _1_2);
  xor xor_5 (xor_5_out, _6_out, _5_out);
  ExactlyOne xor_6 (.out(xor_6_out), .in1(_8_2), .in2(xor_5_out), .in3(_8_2));
  and u__3 (_3_out, _1_2, _2_2);
  ExactlyOne xor_7 (.out(xor_7_out), .in1(_5_out), .in2(_4_2), .in3(_6_out));
  xor xor_8 (xor_8_out, xor_1_out, _3_out);
  ExactlyOne xor_9 (.out(xor_9_out), .in1(_8_2), .in2(xor_8_out), .in3(_8_2));
  ExactlyOne xor_10 (.out(xor_10_out), .in1(_8_2), .in2(xor_7_out), .in3(_8_2));
  and _7_2 (_7_2_out, _4, _2, _1);
  and _6_2 (_6_2_out, _4, _2);
  and _5_2 (_5_2_out, _1, _4);
  and _3_2 (_3_2_out, _1, _2);
  ExactlyOne xor_11 (.out(xor_11_out), .in1(_8_2), .in2(_8_2), .in3(_3_out), .in4(xor_5_out));
  ExactlyOne xor_12 (.out(xor_12_out), .in1(_1_2), .in2(xor_11_out), .in3(_2_2), .in4(_1_2));
  and and_1 (and_1_out, _1, xor_13_out);
  and and_2 (and_2_out, _2, xor_13_out);
  and and_3 (and_3_out, xor_13_out, _4);
  and and_4 (and_4_out, xor_13_out, _8);
  and and_5 (and_5_out, xor_13_out, _1, _2);
  and and_6 (and_6_out, xor_13_out, _4, _1);
  and and_7 (and_7_out, xor_13_out, _4, _2);
  and and_8 (and_8_out, xor_13_out, _4, _2, _1);
  ExactlyOne xor_13 (.out(xor_13_out), .in0(xor_11_out), .in1(_2_2), .in2(_1_2), .in3(_2_2));
  and and_9 (and_9_out, xor_12_out, _1);
  and and_10 (and_10_out, xor_12_out, _2);
  and and_11 (and_11_out, xor_12_out, _4);
  and and_12 (and_12_out, xor_12_out, _3_2_out);
  and and_13 (and_13_out, xor_12_out, _5_2_out);
  and and_14 (and_14_out, xor_12_out, _6_2_out);
  and and_15 (and_15_out, xor_12_out, _7_2_out);
  and and_16 (and_16_out, xor_12_out, _8);
  and and_17 (and_17_out, xor_9_out, _1);
  and and_18 (and_18_out, xor_9_out, _2);
  and and_19 (and_19_out, xor_9_out, _3_2_out);
  and and_20 (and_20_out, xor_9_out, _4);
  and and_21 (and_21_out, xor_9_out, _5_2_out);
  and and_22 (and_22_out, xor_9_out, _6_2_out);
  and and_23 (and_23_out, xor_9_out, _7_2_out);
  and and_24 (and_24_out, xor_9_out, _8);
  and and_25 (and_25_out, _1, xor_10_out);
  and and_26 (and_26_out, xor_10_out, _2);
  and and_27 (and_27_out, xor_10_out, _3_2_out);
  and and_28 (and_28_out, xor_10_out, _4);
  and and_29 (and_29_out, xor_10_out, _5_2_out);
  and and_30 (and_30_out, xor_10_out, _6_2_out);
  and and_31 (and_31_out, xor_10_out, _7_2_out);
  and and_32 (and_32_out, xor_10_out, _8);
  and and_33 (and_33_out, xor_6_out, _1);
  and and_34 (and_34_out, xor_6_out, _2);
  and and_35 (and_35_out, xor_6_out, _3_2_out);
  and and_36 (and_36_out, xor_6_out, _4);
  and and_37 (and_37_out, xor_6_out, _5_2_out);
  and and_38 (and_38_out, xor_6_out, _6_2_out);
  and and_39 (and_39_out, xor_6_out, _7_2_out);
  and and_40 (and_40_out, xor_6_out, _8);
  and and_41 (and_41_out, xor_4_out, _1);
  and and_42 (and_42_out, xor_4_out, _2);
  and and_43 (and_43_out, xor_4_out, _3_2_out);
  and and_44 (and_44_out, xor_4_out, _4);
  and and_45 (and_45_out, xor_4_out, _5_2_out);
  and and_46 (and_46_out, xor_4_out, _6_2_out);
  and and_47 (and_47_out, xor_4_out, _7_2_out);
  and and_48 (and_48_out, xor_4_out, _8);
  and and_49 (and_49_out, xor_1_out, _1);
  and and_50 (and_50_out, xor_1_out, _2);
  and and_51 (and_51_out, xor_1_out, _3_2_out);
  and and_52 (and_52_out, xor_1_out, _4);
  and and_53 (and_53_out, xor_1_out, _5_2_out);
  and and_54 (and_54_out, xor_1_out, _6_2_out);
  and and_55 (and_55_out, xor_1_out, _7_2_out);
  and and_56 (and_56_out, xor_1_out, _8);
  and and_57 (and_57_out, xor_2_out, _1);
  and and_58 (and_58_out, xor_2_out, _2);
  and and_59 (and_59_out, xor_2_out, _3_2_out);
  and and_60 (and_60_out, xor_2_out, _4);
  and and_61 (and_61_out, xor_2_out, _5_2_out);
  and and_62 (and_62_out, xor_2_out, _6_2_out);
  and and_63 (and_63_out, xor_2_out, _7_2_out);
  and and_64 (and_64_out, xor_2_out, _8);
  ExactlyOne xor_14 (.out(_1_3), .in0(and_1_out), .in1(and_5_out), .in2(and_6_out));
  ExactlyOne u__2 (.out(_2_out), .in0(and_2_out), .in1(and_5_out), .in2(and_7_out));
  ExactlyOne u__4 (.out(_4_out), .in0(and_3_out), .in1(and_6_out), .in2(and_7_out));
  buf u__8 (_8_out, and_4_out);  // XOR_Gate
  xor _3_3 (_3_3_out, and_5_out, and_8_out);
  xor _5_3 (_5_3_out, and_6_out, and_8_out);
  xor _6_3 (_6_3_out, and_7_out, and_8_out);
  buf _7_3 (_7_3_out, and_8_out);  // XOR_Gate
  ExactlyOne u__2_2 (.out(_2_2_out), .in1(and_9_out), .in2(and_12_out), .in3(and_13_out));
  ExactlyOne u__4_2 (.out(_4_2_out), .in1(and_10_out), .in2(and_12_out), .in3(and_14_out));
  ExactlyOne u__8_2 (.out(_8_2_out), .in1(and_11_out), .in2(and_13_out), .in3(and_14_out));
  xor _6_4 (_6_4_out, and_12_out, and_15_out);
  xor u__10 (_10_out, and_13_out, and_15_out);
  xor _12 (out_19, and_14_out, and_15_out);
  buf _14 (_14_out, and_15_out);  // XOR_Gate
  buf u__16 (_16_out, and_16_out);  // XOR_Gate
  ExactlyOne _3_4 (.out(_3_4_out), .in1(and_17_out), .in2(and_21_out), .in4(and_19_out));
  ExactlyOne _6_5 (.out(_6_3_out), .in1(and_18_out), .in2(and_22_out), .in4(and_19_out));
  xor u__9 (_9, and_19_out, and_23_out);
  ExactlyOne _12_2 (.out(out_19), .in0(and_20_out), .in1(and_21_out), .in2(and_22_out));
  xor u__15 (_15_out, and_21_out, and_23_out);
  xor u__18 (_18_out, and_22_out, and_23_out);
  buf u__21 (_21_out, and_23_out);  // XOR_Gate
  buf u__24 (_24, and_24_out);  // XOR_Gate
  ExactlyOne u__4_3 (.out(_4_3_out), .in1(and_25_out), .in2(and_27_out), .in3(and_29_out));
  ExactlyOne u__8_3 (.out(_8_3_out), .in1(and_26_out), .in2(and_27_out), .in3(and_30_out));
  or or_2 (out_19, _12_3_out, _12_4_out);
  // OR_Gate or_3 has open pins: in0=_12_3_out, in3=_12_4_out, out=open
  xor _12_3 (_12_3_out, and_27_out, and_31_out);
  ExactlyOne _16_2 (.out(_16_2_out), .in0(and_28_out), .in1(and_29_out), .in2(and_30_out));
  xor u__20 (_20_out, and_29_out, and_31_out);
  or or_4 (_24, _24_2_out, or_8_out);
  xor _24_2 (_24_2_out, and_30_out, and_31_out);
  buf u__28 (_28_out, and_31_out);  // XOR_Gate
  buf u__32 (_32_out, and_32_out);  // XOR_Gate
  ExactlyOne _5_4 (.out(_5_4_out), .in1(and_33_out), .in2(and_35_out), .in3(and_37_out));
  ExactlyOne _10_2 (.out(_10_2_out), .in1(and_34_out), .in2(and_35_out), .in3(and_38_out));
  xor _15_2 (_15_2_out, and_35_out, and_39_out);
  ExactlyOne _20_2 (.out(_20_2_out), .in0(and_36_out), .in1(and_37_out), .in2(and_38_out));
  xor u__25 (_25, and_37_out, and_39_out);
  xor u__30 (_30_out, and_38_out, and_39_out);
  buf u__35 (_35_out, and_39_out);  // XOR_Gate
  buf u__40 (_40_out, and_40_out);  // XOR_Gate
  ExactlyOne _6_6 (.out(_6_6_out), .in1(and_41_out), .in2(and_43_out), .in3(and_45_out));
  ExactlyOne _12_4 (.out(_12_4_out), .in1(and_42_out), .in2(and_43_out), .in3(and_46_out));
  xor _18_2 (_18_2_out, and_43_out, and_47_out);
  ExactlyOne _24_3 (.out(_24_3_out), .in0(and_44_out), .in1(and_45_out), .in2(and_46_out));
  xor _30_2 (_30_2_out, and_45_out, and_47_out);
  xor u__36 (_36, and_46_out, and_47_out);
  buf u__42 (_42_out, and_47_out);  // XOR_Gate
  buf u__48 (_48_out, and_48_out);  // XOR_Gate
  ExactlyOne _7_4 (.out(_7_4_out), .in1(and_49_out), .in2(and_51_out), .in3(and_53_out));
  ExactlyOne _14_2 (.out(_14_2_out), .in1(and_50_out), .in2(and_51_out), .in3(and_54_out));
  xor _21_2 (_21_2_out, and_51_out, and_55_out);
  ExactlyOne _28_2 (.out(_28_2_out), .in0(and_52_out), .in1(and_53_out), .in2(and_54_out));
  xor _35_2 (_35_2_out, and_53_out, and_55_out);
  xor _42_2 (_42_2_out, and_54_out, and_55_out);
  buf u__49 (_49, and_55_out);  // XOR_Gate
  buf u__56 (_56_out, and_56_out);  // XOR_Gate
  ExactlyOne _8_4 (.out(_8_4_out), .in1(and_57_out), .in2(and_59_out), .in3(and_61_out));
  ExactlyOne _16_3 (.out(_16_3_out), .in1(and_58_out), .in2(and_59_out), .in3(and_62_out));
  xor _24_4 (_24_4_out, and_59_out, and_63_out);
  ExactlyOne _32_2 (.out(_32_2_out), .in0(and_60_out), .in1(and_61_out), .in2(and_62_out));
  xor _40_2 (_40_2_out, and_61_out, and_63_out);
  xor _48_2 (_48_2_out, and_62_out, and_63_out);
  buf _56_2 (_56_2_out, and_63_out);  // XOR_Gate
  buf u__64 (_64, and_64_out);  // XOR_Gate
  or or_5 (or_5_out, _8_4_out, _8_3_out);
  or or_6 (_15, _15_out, _15_2_out);
  or or_7 (_18, _18_out, _18_2_out);
  or or_8 (or_8_out, _24_3_out, _24_4_out);
  or or_9 (_30, _30_out, _30_2_out);
  or or_10 (_56, _56_2_out, _56_out);
  or or_11 (or_11_out, _16_2_out, _16_3_out);
  or or_12 (or_12_out, _4_2_out, _4_3_out);
  or or_13 (_16, _16_out, or_11_out);
  or or_14 (_20, _20_out, _20_2_out);
  or or_15 (_28, _28_out, _28_2_out);
  or or_16 (_42, _42_out, _42_2_out);
  or or_17 (or_17_out, _6_3_out, _6_6_out);
  or or_18 (or_18_out, or_5_out, _8_2_out);
  or or_19 (_21, _21_out, _21_2_out);
  or or_20 (_7, _7_3_out, _7_4_out);
  or or_21 (_10, _10_2_out, _10_out);
  or or_22 (_5, _5_3_out, _5_4_out);
  or or_23 (out_20, _14_out, _14_2_out);
  or or_24 (_35, _35_out, _35_2_out);
  or or_25 (_3, _3_3_out, _3_4_out);
  or or_26 (_4_3, _4_out, or_12_out);
  or or_27 (_40, _40_out, _40_2_out);
  or or_28 (_6, or_17_out, _6_4_out);
  or or_29 (_2_3, _2_out, _2_2_out);
  or or_30 (_8_3, _8_out, or_18_out);
  or or_31 (_48, _48_out, _48_2_out);
  or or_32 (_32, _32_out, _32_2_out);

  // Notes on the sheet:
  //   4
  //   1
  //   30 possibilités
endmodule
